// Logisim project adders.circ as structural Verilog: 5 circuits, main circuit HalfAdder
module HalfAdder (
  input  Input_1,
  input  Input_2,
  output Sum,
  output Carry
);

  xor xor_1 (Sum, Input_1, Input_2);
  and and_1 (Carry, Input_1, Input_2);
endmodule

// FullAdder
module FullAddder (
  input  Input_1,
  input  Input_2,
  input  Input_3,
  output Sum,
  output Carry
);

  wire and_1_out, and_2_out, xor_1_out;

  xor xor_1 (xor_1_out, Input_1, Input_2);
  and and_1 (and_1_out, Input_1, Input_2);
  xor xor_2 (Sum, xor_1_out, Input_3);
  and and_2 (and_2_out, xor_1_out, Input_3);
  or or_1 (Carry, and_2_out, and_1_out);
endmodule

module Add16 (
  input  [15:0] Input_2,
  input  [15:0] Input_1,
  output [15:0] Result
);

  wire fulladdder_1_carry, fulladdder_2_carry, fulladdder_3_carry, fulladdder_4_carry, fulladdder_5_carry,
       fulladdder_6_carry, fulladdder_7_carry, fulladdder_8_carry, fulladdder_9_carry, fulladdder_10_carry,
       fulladdder_11_carry, fulladdder_12_carry, fulladdder_13_carry, fulladdder_14_carry,
       fulladdder_15_carry, fulladdder_16_carry, undriven;

  FullAddder fulladdder_1 (
    .Input_1(Input_1[0]), .Input_2(Input_2[0]), .Input_3(undriven), .Sum(Result[0]),
    .Carry(fulladdder_1_carry));
  FullAddder fulladdder_2 (
    .Input_1(Input_1[1]), .Input_2(Input_2[1]), .Input_3(fulladdder_1_carry), .Sum(Result[1]),
    .Carry(fulladdder_2_carry));
  FullAddder fulladdder_3 (
    .Input_1(Input_1[2]), .Input_2(Input_2[2]), .Input_3(fulladdder_2_carry), .Sum(Result[2]),
    .Carry(fulladdder_3_carry));
  FullAddder fulladdder_4 (
    .Input_1(Input_1[3]), .Input_2(Input_2[3]), .Input_3(fulladdder_3_carry), .Sum(Result[3]),
    .Carry(fulladdder_4_carry));
  FullAddder fulladdder_5 (
    .Input_1(Input_1[4]), .Input_2(Input_2[4]), .Input_3(fulladdder_4_carry), .Sum(Result[4]),
    .Carry(fulladdder_5_carry));
  FullAddder fulladdder_6 (
    .Input_1(Input_1[5]), .Input_2(Input_2[5]), .Input_3(fulladdder_5_carry), .Sum(Result[5]),
    .Carry(fulladdder_6_carry));
  FullAddder fulladdder_7 (
    .Input_1(Input_1[6]), .Input_2(Input_2[6]), .Input_3(fulladdder_6_carry), .Sum(Result[6]),
    .Carry(fulladdder_7_carry));
  FullAddder fulladdder_8 (
    .Input_1(Input_1[7]), .Input_2(Input_2[7]), .Input_3(fulladdder_7_carry), .Sum(Result[7]),
    .Carry(fulladdder_8_carry));
  FullAddder fulladdder_9 (
    .Input_1(Input_1[8]), .Input_2(Input_2[8]), .Input_3(fulladdder_8_carry), .Sum(Result[8]),
    .Carry(fulladdder_9_carry));
  FullAddder fulladdder_10 (
    .Input_1(Input_1[9]), .Input_2(Input_2[9]), .Input_3(fulladdder_9_carry), .Sum(Result[9]),
    .Carry(fulladdder_10_carry));
  FullAddder fulladdder_11 (
    .Input_1(Input_1[10]), .Input_2(Input_2[10]), .Input_3(fulladdder_10_carry), .Sum(Result[10]),
    .Carry(fulladdder_11_carry));
  FullAddder fulladdder_12 (
    .Input_1(Input_1[11]), .Input_2(Input_2[11]), .Input_3(fulladdder_11_carry), .Sum(Result[11]),
    .Carry(fulladdder_12_carry));
  FullAddder fulladdder_13 (
    .Input_1(Input_1[12]), .Input_2(Input_2[12]), .Input_3(fulladdder_12_carry), .Sum(Result[12]),
    .Carry(fulladdder_13_carry));
  FullAddder fulladdder_14 (
    .Input_1(Input_1[13]), .Input_2(Input_2[13]), .Input_3(fulladdder_13_carry), .Sum(Result[13]),
    .Carry(fulladdder_14_carry));
  FullAddder fulladdder_15 (
    .Input_1(Input_1[14]), .Input_2(Input_2[14]), .Input_3(fulladdder_14_carry), .Sum(Result[14]),
    .Carry(fulladdder_15_carry));
  FullAddder fulladdder_16 (
    .Input_1(Input_1[15]), .Input_2(Input_2[15]), .Input_3(fulladdder_15_carry), .Sum(Result[15]),
    .Carry(fulladdder_16_carry));
endmodule

module ALU (
  input  [15:0] X,
  input  [15:0] Y,
  input  ZX,
  input  NX,
  input  ZY,
  input  NY,
  input  F,
  input  NO,
  output [15:0] Output_1,
  output ZR,
  output NG
);

  wire or8way_1_output, or8way_2_output, or_1_output;
  wire [15:0] add16_1_result, and16_1_output_16_bit, mux16_1_output_16_bit, mux16_2_output_16_bit,
       mux16_3_output_16_bit, mux16_4_output_16_bit, mux16_5_output_16_bit, not16_1_output_16_bit,
       not16_2_output_16_bit, not16_3_output_16_bit;

  MUX16 mux16_1 (
    .Input_16_bit_1(X), .Input_16_bit_2({16{1'b0}}), .Select_Bit(ZX), .Output_16_bit(mux16_1_output_16_bit));
  NOT16 not16_1 (.Input_16_bit(mux16_1_output_16_bit), .Output_16_bit(not16_1_output_16_bit));
  MUX16 mux16_2 (
    .Input_16_bit_1(mux16_1_output_16_bit), .Input_16_bit_2(not16_1_output_16_bit), .Select_Bit(NX),
    .Output_16_bit(mux16_2_output_16_bit));
  MUX16 mux16_3 (
    .Input_16_bit_1(Y), .Input_16_bit_2({16{1'b0}}), .Select_Bit(ZY), .Output_16_bit(mux16_3_output_16_bit));
  NOT16 not16_2 (.Input_16_bit(mux16_3_output_16_bit), .Output_16_bit(not16_2_output_16_bit));
  OR8WAY or8way_1 (.Input_8_bit(Output_1[7:0]), .Output(or8way_1_output));
  OR8WAY or8way_2 (.Input_8_bit({NG, Output_1[14:8]}), .Output(or8way_2_output));
  MUX16 mux16_4 (
    .Input_16_bit_1(mux16_3_output_16_bit), .Input_16_bit_2(not16_2_output_16_bit), .Select_Bit(NY),
    .Output_16_bit(mux16_4_output_16_bit));
  OR or_1 (.Input_1(or8way_1_output), .Input_2(or8way_2_output), .Output(or_1_output));
  NOT not_1 (.Input(or_1_output), .Output(ZR));
  AND16 and16_1 (
    .Input_16_bit_1(mux16_2_output_16_bit), .Input_16_bit_2(mux16_4_output_16_bit),
    .Output_16_bit(and16_1_output_16_bit));
  Add16 add16_1 (.Input_2(mux16_2_output_16_bit), .Input_1(mux16_4_output_16_bit), .Result(add16_1_result));
  MUX16 mux16_5 (
    .Input_16_bit_1(and16_1_output_16_bit), .Input_16_bit_2(add16_1_result), .Select_Bit(F),
    .Output_16_bit(mux16_5_output_16_bit));
  NOT16 not16_3 (.Input_16_bit(mux16_5_output_16_bit), .Output_16_bit(not16_3_output_16_bit));
  MUX16 mux16_6 (
    .Input_16_bit_1(mux16_5_output_16_bit), .Input_16_bit_2(not16_3_output_16_bit), .Select_Bit(NO),
    .Output_16_bit({NG, Output_1[14:0]}));

  assign Output_1[15] = NG;
endmodule

module INC16 (
  input  [15:0] Input_1,
  output [15:0] Output_1
);

  Add16 add16_1 (.Input_2(16'h1), .Input_1(Input_1), .Result(Output_1));
endmodule
