// Logisim project LogicGates.circ as structural Verilog: 16 circuits, main circuit NOT
module NOT (
  input  Input,
  output Output
);

  nand nand_1 (Output, Input, Input);
endmodule

module AND (
  input  Input_1,
  input  Input_2,
  output Output
);

  wire nand_1_out;

  nand nand_1 (nand_1_out, Input_1, Input_2);
  not not_1 (Output, nand_1_out);
endmodule

module OR (
  input  Input_1,
  input  Input_2,
  output Output
);

  wire and_1_out, not_1_out, not_2_out;

  not not_1 (not_1_out, Input_1);
  not not_2 (not_2_out, Input_2);
  and and_1 (and_1_out, not_1_out, not_2_out);
  not not_3 (Output, and_1_out);
endmodule

module XOR (
  input  Input_1,
  input  Input_2,
  output Output
);

  wire nand_1_out, or_1_out;

  nand nand_1 (nand_1_out, Input_1, Input_2);
  or or_1 (or_1_out, Input_1, Input_2);
  and and_1 (Output, nand_1_out, or_1_out);
endmodule

module NAND (
  input  Input_1,
  input  Input_2,
  output Output
);

  nand nand_1 (Output, Input_1, Input_2);
endmodule

module MUX (
  input  Input_1,
  input  Select_Bit,
  input  Input_2,
  output Output
);

  wire and_1_out, and_2_out, and_3_out, and_4_out, not_1_out, not_2_out, not_3_out;

  and and_1 (and_1_out, Select_Bit, Select_Bit);
  not not_1 (not_1_out, and_1_out);
  and and_2 (and_2_out, Input_1, Select_Bit);
  and and_3 (and_3_out, not_1_out, Input_2);
  not not_2 (not_2_out, and_2_out);
  not not_3 (not_3_out, and_3_out);
  and and_4 (and_4_out, not_2_out, not_3_out);
  not not_4 (Output, and_4_out);
endmodule

module DMUX (
  input  Input,
  input  Select_Bit,
  output Output_1,
  output Output_2
);

  wire and_1_out, and_2_out, and_3_out, and_4_out, and_5_out, not_1_out, not_2_out, not_3_out;

  not not_1 (not_1_out, and_1_out);
  and and_1 (and_1_out, Select_Bit, Select_Bit);
  and and_2 (and_2_out, Input, not_1_out);
  and and_3 (and_3_out, Select_Bit, Input);
  not not_2 (not_2_out, and_2_out);
  not not_3 (not_3_out, and_3_out);
  and and_4 (and_4_out, not_2_out, not_2_out);
  and and_5 (and_5_out, not_3_out, not_3_out);
  not not_4 (Output_1, and_4_out);
  not not_5 (Output_2, and_5_out);
endmodule

module NOT16 (
  input  [15:0] Input_16_bit,
  output [15:0] Output_16_bit
);

  not not_1 (Output_16_bit[0], Input_16_bit[0]);
  not not_2 (Output_16_bit[1], Input_16_bit[1]);
  not not_3 (Output_16_bit[4], Input_16_bit[4]);
  not not_4 (Output_16_bit[5], Input_16_bit[5]);
  not not_5 (Output_16_bit[8], Input_16_bit[8]);
  not not_6 (Output_16_bit[9], Input_16_bit[9]);
  not not_7 (Output_16_bit[12], Input_16_bit[12]);
  not not_8 (Output_16_bit[13], Input_16_bit[13]);
  not not_9 (Output_16_bit[2], Input_16_bit[2]);
  not not_10 (Output_16_bit[3], Input_16_bit[3]);
  not not_11 (Output_16_bit[6], Input_16_bit[6]);
  not not_12 (Output_16_bit[7], Input_16_bit[7]);
  not not_13 (Output_16_bit[10], Input_16_bit[10]);
  not not_14 (Output_16_bit[11], Input_16_bit[11]);
  not not_15 (Output_16_bit[14], Input_16_bit[14]);
  not not_16 (Output_16_bit[15], Input_16_bit[15]);
endmodule

module AND16 (
  input  [15:0] Input_16_bit_1,
  input  [15:0] Input_16_bit_2,
  output [15:0] Output_16_bit
);

  assign Output_16_bit = Input_16_bit_1 & Input_16_bit_2;  // AND_Gate AND, 16 bits wide
endmodule

module OR16 (
  input  [15:0] Input_16_bit_1,
  input  [15:0] Input_16_bit_2,
  output [15:0] Output_16
);

  assign Output_16 = Input_16_bit_1 | Input_16_bit_2;  // OR_Gate OR, 16 bits wide
endmodule

module MUX16 (
  input  [15:0] Input_16_bit_1,
  input  [15:0] Input_16_bit_2,
  input  Select_Bit,
  output [15:0] Output_16_bit
);

  Multiplexer #(.width(16), .enable("false")) multiplexer_1 (
    .in0(Input_16_bit_1), .in1(Input_16_bit_2), .out(Output_16_bit), .sel(Select_Bit));
endmodule

module OR8WAY (
  input  [7:0] Input_8_bit,
  output Output
);

  or OR8WAY (Output, Input_8_bit[0], Input_8_bit[1], Input_8_bit[2], Input_8_bit[3], Input_8_bit[4], Input_8_bit[5], Input_8_bit[6], Input_8_bit[7]);
endmodule

module MUX4WAY16 (
  input  [15:0] Input_16_bit_1,
  input  [15:0] Input_16_bit_2,
  input  [15:0] Input_16_bit_3,
  input  [15:0] Input_16_bit_4,
  input  [1:0] Select_2_Bit,
  output [15:0] Output_16
);

  Multiplexer #(.select(2), .width(16), .enable("false")) multiplexer_1 (
    .in0(Input_16_bit_1), .in1(Input_16_bit_2), .in2(Input_16_bit_3), .in3(Input_16_bit_4), .out(Output_16),
    .sel(Select_2_Bit));
endmodule

module MUX8WAY16 (
  input  [15:0] Input_16_bit_1,
  input  [15:0] Input_16_bit_2,
  input  [15:0] Input_16_bit_3,
  input  [15:0] Input_16_bit_4,
  input  [15:0] Input_16_bit_5,
  input  [15:0] Input_16_bit_6,
  input  [15:0] Input_16_bit_7,
  input  [2:0] Select_3_bit,
  input  [15:0] Input_16_bit_8,
  output [15:0] Output_16_bit
);

  Multiplexer #(.select(3), .width(16), .enable("false")) multiplexer_1 (
    .in0(Input_16_bit_1), .in1(Input_16_bit_2), .in2(Input_16_bit_3), .in3(Input_16_bit_4),
    .in4(Input_16_bit_5), .in5(Input_16_bit_6), .in6(Input_16_bit_7), .in7(Input_16_bit_8),
    .out(Output_16_bit), .sel(Select_3_bit));
endmodule

module DMUX4WAY (
  input  Input,
  input  [1:0] Select_2_bit,
  output Output_1,
  output Output_2,
  output Output_3,
  output Output_4
);

  Demultiplexer #(.select(2), .enable("false")) demultiplexer_1 (
    .out0(Output_1), .out1(Output_2), .out2(Output_3), .out3(Output_4), .in(Input), .sel(Select_2_bit));
endmodule

module DMUX8WAY (
  input  Input,
  input  [2:0] Select_3_Bits,
  output Output_1,
  output Output_2,
  output Output_3,
  output Output_4,
  output Output_5,
  output Output_6,
  output Output_7,
  output Output_8
);

  Demultiplexer #(.select(3), .enable("false")) demultiplexer_1 (
    .out0(Output_1), .out1(Output_2), .out2(Output_3), .out3(Output_4), .out4(Output_5), .out5(Output_6),
    .out6(Output_7), .out7(Output_8), .in(Input), .sel(Select_3_Bits));
endmodule
