// Logisim project memory.circ as structural Verilog: 6 circuits, main circuit BIT
module BIT (
  input  Input_1,
  input  Load,
  output Output_1
);

  wire Clck_out, multiplexer_1_out;

  Multiplexer multiplexer_1 (.in0(Output_1), .in1(Input_1), .out(multiplexer_1_out), .sel(Load));
  D_Flip_Flop d_ff_1 (.D(multiplexer_1_out), .clk(Clck_out), .Q(Output_1), .preset(1'b0), .reset(1'b0));  // open: Qn
  Clock Clck (.out(Clck_out));
endmodule

module regsiter (
  input  Load,
  input  [15:0] Input_1,
  output [15:0] Output_1
);

  BIT bit_1 (.Input_1(Input_1[0]), .Load(Load), .Output_1(Output_1[0]));
  BIT bit_2 (.Input_1(Input_1[1]), .Load(Load), .Output_1(Output_1[1]));
  BIT bit_3 (.Input_1(Input_1[2]), .Load(Load), .Output_1(Output_1[2]));
  BIT bit_4 (.Input_1(Input_1[3]), .Load(Load), .Output_1(Output_1[3]));
  BIT bit_5 (.Input_1(Input_1[4]), .Load(Load), .Output_1(Output_1[4]));
  BIT bit_6 (.Input_1(Input_1[5]), .Load(Load), .Output_1(Output_1[5]));
  BIT bit_7 (.Input_1(Input_1[6]), .Load(Load), .Output_1(Output_1[6]));
  BIT bit_8 (.Input_1(Input_1[7]), .Load(Load), .Output_1(Output_1[7]));
  BIT bit_9 (.Input_1(Input_1[8]), .Load(Load), .Output_1(Output_1[8]));
  BIT bit_10 (.Input_1(Input_1[9]), .Load(Load), .Output_1(Output_1[9]));
  BIT bit_11 (.Input_1(Input_1[10]), .Load(Load), .Output_1(Output_1[10]));
  BIT bit_12 (.Input_1(Input_1[11]), .Load(Load), .Output_1(Output_1[11]));
  BIT bit_13 (.Input_1(Input_1[12]), .Load(Load), .Output_1(Output_1[12]));
  BIT bit_14 (.Input_1(Input_1[13]), .Load(Load), .Output_1(Output_1[13]));
  BIT bit_15 (.Input_1(Input_1[14]), .Load(Load), .Output_1(Output_1[14]));
  BIT bit_16 (.Input_1(Input_1[15]), .Load(Load), .Output_1(Output_1[15]));
endmodule

module RAM8 (
  input  [15:0] Input_1,
  input  Load,
  input  [2:0] Address,
  output [15:0] Output_1
);

  wire dmux8way_1_output_1, dmux8way_1_output_2, dmux8way_1_output_3, dmux8way_1_output_4,
       dmux8way_1_output_5, dmux8way_1_output_6, dmux8way_1_output_7, dmux8way_1_output_8;
  wire [15:0] regsiter_1_output_1, regsiter_2_output_1, regsiter_3_output_1, regsiter_4_output_1,
       regsiter_5_output_1, regsiter_6_output_1, regsiter_7_output_1, regsiter_8_output_1;

  DMUX8WAY dmux8way_1 (
    .Input(Load), .Select_3_Bits(Address), .Output_1(dmux8way_1_output_1), .Output_2(dmux8way_1_output_2),
    .Output_3(dmux8way_1_output_3), .Output_4(dmux8way_1_output_4), .Output_5(dmux8way_1_output_5),
    .Output_6(dmux8way_1_output_6), .Output_7(dmux8way_1_output_7), .Output_8(dmux8way_1_output_8));
  regsiter regsiter_1 (.Load(dmux8way_1_output_1), .Input_1(Input_1), .Output_1(regsiter_1_output_1));
  regsiter regsiter_2 (.Load(dmux8way_1_output_2), .Input_1(Input_1), .Output_1(regsiter_2_output_1));
  regsiter regsiter_3 (.Load(dmux8way_1_output_3), .Input_1(Input_1), .Output_1(regsiter_3_output_1));
  regsiter regsiter_4 (.Load(dmux8way_1_output_4), .Input_1(Input_1), .Output_1(regsiter_4_output_1));
  regsiter regsiter_5 (.Load(dmux8way_1_output_5), .Input_1(Input_1), .Output_1(regsiter_5_output_1));
  regsiter regsiter_6 (.Load(dmux8way_1_output_6), .Input_1(Input_1), .Output_1(regsiter_6_output_1));
  regsiter regsiter_7 (.Load(dmux8way_1_output_7), .Input_1(Input_1), .Output_1(regsiter_7_output_1));
  regsiter regsiter_8 (.Load(dmux8way_1_output_8), .Input_1(Input_1), .Output_1(regsiter_8_output_1));
  MUX8WAY16 mux8way16_1 (
    .Input_16_bit_1(regsiter_1_output_1), .Input_16_bit_2(regsiter_2_output_1),
    .Input_16_bit_3(regsiter_3_output_1), .Input_16_bit_4(regsiter_4_output_1),
    .Input_16_bit_5(regsiter_5_output_1), .Input_16_bit_6(regsiter_6_output_1),
    .Input_16_bit_7(regsiter_7_output_1), .Input_16_bit_8(regsiter_8_output_1), .Select_3_bit(Address),
    .Output_16_bit(Output_1));
endmodule

module RAM64 (
  input  [15:0] Input_1,
  input  Load,
  input  [5:0] Address,
  output [15:0] Output_1
);

  wire dmux8way_1_output_1, dmux8way_1_output_2, dmux8way_1_output_3, dmux8way_1_output_4,
       dmux8way_1_output_5, dmux8way_1_output_6, dmux8way_1_output_7, dmux8way_1_output_8;
  wire [15:0] ram8_1_output_1, ram8_2_output_1, ram8_3_output_1, ram8_4_output_1, ram8_5_output_1,
       ram8_6_output_1, ram8_7_output_1, ram8_8_output_1;

  DMUX8WAY dmux8way_1 (
    .Input(Load), .Select_3_Bits(Address[5:3]), .Output_1(dmux8way_1_output_1),
    .Output_2(dmux8way_1_output_2), .Output_3(dmux8way_1_output_3), .Output_4(dmux8way_1_output_4),
    .Output_5(dmux8way_1_output_5), .Output_6(dmux8way_1_output_6), .Output_7(dmux8way_1_output_7),
    .Output_8(dmux8way_1_output_8));
  RAM8 ram8_1 (.Input_1(Input_1), .Load(dmux8way_1_output_1), .Address(Address[2:0]), .Output_1(ram8_1_output_1));
  RAM8 ram8_2 (.Input_1(Input_1), .Load(dmux8way_1_output_2), .Address(Address[2:0]), .Output_1(ram8_2_output_1));
  RAM8 ram8_3 (.Input_1(Input_1), .Load(dmux8way_1_output_3), .Address(Address[2:0]), .Output_1(ram8_3_output_1));
  RAM8 ram8_4 (.Input_1(Input_1), .Load(dmux8way_1_output_4), .Address(Address[2:0]), .Output_1(ram8_4_output_1));
  RAM8 ram8_5 (.Input_1(Input_1), .Load(dmux8way_1_output_5), .Address(Address[2:0]), .Output_1(ram8_5_output_1));
  RAM8 ram8_6 (.Input_1(Input_1), .Load(dmux8way_1_output_6), .Address(Address[2:0]), .Output_1(ram8_6_output_1));
  RAM8 ram8_7 (.Input_1(Input_1), .Load(dmux8way_1_output_7), .Address(Address[2:0]), .Output_1(ram8_7_output_1));
  RAM8 ram8_8 (.Input_1(Input_1), .Load(dmux8way_1_output_8), .Address(Address[2:0]), .Output_1(ram8_8_output_1));
  MUX8WAY16 mux8way16_1 (
    .Input_16_bit_1(ram8_1_output_1), .Input_16_bit_2(ram8_2_output_1), .Input_16_bit_3(ram8_3_output_1),
    .Input_16_bit_4(ram8_4_output_1), .Input_16_bit_5(ram8_5_output_1), .Input_16_bit_6(ram8_6_output_1),
    .Input_16_bit_7(ram8_7_output_1), .Input_16_bit_8(ram8_8_output_1), .Select_3_bit(Address[5:3]),
    .Output_16_bit(Output_1));
endmodule

module RAM512 (
  input  [15:0] Input_1,
  input  Load,
  input  [8:0] Address,
  output [15:0] Output_1
);

  wire dmux8way_1_output_1, dmux8way_1_output_2, dmux8way_1_output_3, dmux8way_1_output_4,
       dmux8way_1_output_5, dmux8way_1_output_6, dmux8way_1_output_7, dmux8way_1_output_8;
  wire [15:0] ram64_1_output_1, ram64_2_output_1, ram64_3_output_1, ram64_4_output_1, ram64_5_output_1,
       ram64_6_output_1, ram64_7_output_1, ram64_8_output_1;

  DMUX8WAY dmux8way_1 (
    .Input(Load), .Select_3_Bits(Address[8:6]), .Output_1(dmux8way_1_output_1),
    .Output_2(dmux8way_1_output_2), .Output_3(dmux8way_1_output_3), .Output_4(dmux8way_1_output_4),
    .Output_5(dmux8way_1_output_5), .Output_6(dmux8way_1_output_6), .Output_7(dmux8way_1_output_7),
    .Output_8(dmux8way_1_output_8));
  RAM64 ram64_1 (.Input_1(Input_1), .Load(dmux8way_1_output_1), .Address(Address[5:0]), .Output_1(ram64_1_output_1));
  RAM64 ram64_2 (.Input_1(Input_1), .Load(dmux8way_1_output_2), .Address(Address[5:0]), .Output_1(ram64_2_output_1));
  RAM64 ram64_3 (.Input_1(Input_1), .Load(dmux8way_1_output_3), .Address(Address[5:0]), .Output_1(ram64_3_output_1));
  RAM64 ram64_4 (.Input_1(Input_1), .Load(dmux8way_1_output_4), .Address(Address[5:0]), .Output_1(ram64_4_output_1));
  RAM64 ram64_5 (.Input_1(Input_1), .Load(dmux8way_1_output_5), .Address(Address[5:0]), .Output_1(ram64_5_output_1));
  RAM64 ram64_6 (.Input_1(Input_1), .Load(dmux8way_1_output_6), .Address(Address[5:0]), .Output_1(ram64_6_output_1));
  RAM64 ram64_7 (.Input_1(Input_1), .Load(dmux8way_1_output_7), .Address(Address[5:0]), .Output_1(ram64_7_output_1));
  RAM64 ram64_8 (.Input_1(Input_1), .Load(dmux8way_1_output_8), .Address(Address[5:0]), .Output_1(ram64_8_output_1));
  MUX8WAY16 mux8way16_1 (
    .Input_16_bit_1(ram64_1_output_1), .Input_16_bit_2(ram64_2_output_1), .Input_16_bit_3(ram64_3_output_1),
    .Input_16_bit_4(ram64_4_output_1), .Input_16_bit_5(ram64_5_output_1), .Input_16_bit_6(ram64_6_output_1),
    .Input_16_bit_7(ram64_7_output_1), .Input_16_bit_8(ram64_8_output_1), .Select_3_bit(Address[8:6]),
    .Output_16_bit(Output_1));
endmodule

module PC (
  input  Reset,
  input  [15:0] Input_1,
  input  Load,
  input  INC,
  output [15:0] Output_1
);

  wire [15:0] inc16_1_output_1, mux16_1_output_16_bit, mux16_2_output_16_bit, mux16_3_output_16_bit;

  INC16 inc16_1 (.Input_1(Output_1), .Output_1(inc16_1_output_1));
  MUX16 mux16_1 (
    .Input_16_bit_1(Output_1), .Input_16_bit_2(inc16_1_output_1), .Select_Bit(INC),
    .Output_16_bit(mux16_1_output_16_bit));
  MUX16 mux16_2 (
    .Input_16_bit_1(mux16_1_output_16_bit), .Input_16_bit_2(Input_1), .Select_Bit(Load),
    .Output_16_bit(mux16_2_output_16_bit));
  MUX16 mux16_3 (
    .Input_16_bit_1(mux16_2_output_16_bit), .Input_16_bit_2({16{1'b0}}), .Select_Bit(Reset),
    .Output_16_bit(mux16_3_output_16_bit));
  regsiter regsiter_1 (.Load(1'b1), .Input_1(mux16_3_output_16_bit), .Output_1(Output_1));
endmodule
