// Logisim project logic-gates.circ as structural Verilog: 16 circuits, main circuit NOT
module NOT (
  input  in_1,
  output out_2
);

  not not_1 (out_2, in_1);
endmodule

module AND (
  input  in_1,
  input  in_2,
  output out_3
);

  and and_1 (out_3, in_1, in_2);
endmodule

module OR (
  input  in_1,
  input  in_2,
  output out_3
);

  or or_1 (out_3, in_1, in_2);
endmodule

module XOR (
  input  in_1,
  input  in_2,
  output out_3
);

  wire nand_1_out, or_1_out;

  or or_1 (or_1_out, in_1, in_2);
  nand nand_1 (nand_1_out, in_1, in_2);
  and and_1 (out_3, or_1_out, nand_1_out);
endmodule

module NAND (
  input  in_1,
  input  in_2,
  output out_3
);

  nand nand_1 (out_3, in_1, in_2);
endmodule

module MUX (
  input  Input_1,
  input  select_bit,
  input  Input_2,
  output out_4
);

  wire nand_1_out, nand_2_out, nand_3_out;

  nand nand_1 (nand_1_out, select_bit, select_bit);
  nand nand_2 (nand_2_out, Input_1, select_bit);
  nand nand_3 (nand_3_out, nand_1_out, Input_2);
  nand nand_4 (out_4, nand_2_out, nand_3_out);
endmodule

module DMUX (
  input  Input,
  input  Select_Bit,
  output out_3,
  output out_4
);

  wire nand_1_out, nand_2_out, nand_3_out;

  nand nand_1 (nand_1_out, Select_Bit, Select_Bit);
  nand nand_2 (nand_2_out, Input, nand_1_out);
  nand nand_3 (nand_3_out, Select_Bit, Input);
  nand nand_4 (out_3, nand_2_out, nand_2_out);
  nand nand_5 (out_4, nand_3_out, nand_3_out);
endmodule

module NOT16 (
  input  [15:0] in_1,
  output [15:0] out_2
);

  not not_1 (out_2[0], in_1[0]);
  not not_2 (out_2[4], in_1[4]);
  not not_3 (out_2[8], in_1[8]);
  not not_4 (out_2[12], in_1[12]);
  not not_5 (out_2[1], in_1[1]);
  not not_6 (out_2[2], in_1[2]);
  not not_7 (out_2[5], in_1[5]);
  not not_8 (out_2[6], in_1[6]);
  not not_9 (out_2[9], in_1[9]);
  not not_10 (out_2[10], in_1[10]);
  not not_11 (out_2[13], in_1[13]);
  not not_12 (out_2[14], in_1[14]);
  not not_13 (out_2[3], in_1[3]);
  not not_14 (out_2[7], in_1[7]);
  not not_15 (out_2[11], in_1[11]);
  not not_16 (out_2[15], in_1[15]);
endmodule

module AND16 (
  input  [15:0] in_1,
  input  [15:0] in_2,
  output [15:0] out_3
);

  assign out_3 = in_1 & in_2;  // AND_Gate and_1, 16 bits wide
endmodule

module OR16 (
  input  [15:0] in_1,
  input  [15:0] in_2,
  output [15:0] out_3
);

  assign out_3 = in_1 | in_2;  // OR_Gate or_1, 16 bits wide
endmodule

module MUX16 (
  input  [15:0] in_1,
  input  [15:0] in_2,
  input  in_3,
  output [15:0] out_4
);

  Multiplexer #(.width(16)) multiplexer_1 (.in0(in_1), .in1(in_2), .out(out_4), .sel(in_3));  // open: en
endmodule

module OR8WAY (
  input  [7:0] in_1,
  output out_2
);

  or OR8WAY (out_2, in_1[0], in_1[1], in_1[2], in_1[3], in_1[4], in_1[5], in_1[6], in_1[7]);
endmodule

module MUX4WAY16 (
  input  [15:0] in_1,
  input  [15:0] in_2,
  input  [15:0] in_3,
  input  [15:0] in_4,
  input  [1:0] in_5,
  output [15:0] out_6
);

  Multiplexer #(.select(2), .width(16)) multiplexer_1 (
    .in0(in_1), .in1(in_2), .in2(in_3), .in3(in_4), .out(out_6), .sel(in_5));  // open: en
endmodule

module MUX8WAY16 (
  input  [15:0] in_1,
  input  [15:0] in_2,
  input  [15:0] in_3,
  input  [15:0] in_4,
  input  [15:0] in_5,
  input  [15:0] in_6,
  input  [15:0] in_7,
  input  [2:0] in_8,
  input  [15:0] in_9,
  output [15:0] out_10
);

  Multiplexer #(.select(3), .width(16)) multiplexer_1 (
    .in0(in_1), .in1(in_2), .in2(in_3), .in3(in_4), .in4(in_5), .in5(in_6), .in6(in_7), .in7(in_9),
    .out(out_10), .sel(in_8));  // open: en
endmodule

module DMUX4WAY (
  input  in_1,
  input  [1:0] in_2,
  output out_3,
  output out_4,
  output out_5,
  output out_6
);

  Demultiplexer #(.select(2)) demultiplexer_1 (
    .out0(out_3), .out1(out_4), .out2(out_5), .out3(out_6), .in(in_1), .sel(in_2));  // open: en
endmodule

module DMUX8WAY (
  input  in_1,
  input  [2:0] in_2,
  output out_3,
  output out_4,
  output out_5,
  output out_6,
  output out_7,
  output out_8,
  output out_9,
  output out_10
);

  Demultiplexer #(.select(3)) demultiplexer_1 (
    .out0(out_3), .out1(out_4), .out2(out_5), .out3(out_6), .out4(out_7), .out5(out_8), .out6(out_9),
    .out7(out_10), .in(in_1), .sel(in_2));  // open: en
endmodule
